// Logisim project Deimos.circ as structural Verilog: 3 circuits, main circuit main
module main (
);

  // DualRAM #(.addrWidth(16)) dualram_1: pin names not known
endmodule

module arithmetic_logic_unit (
  input  [3:0] O,
  input  [15:0] A,
  input  [15:0] B,
  output [15:0] Y
);

  wire [7:0] adder_1_out, and_1_out, divider_1_out, not_1_out, or_1_out, subtractor_1_out, xor_1_out;
  wire [15:0] and_2_out, bit_extender_1_out, bit_extender_2_out, bit_extender_3_out, bit_extender_4_out,
       bit_extender_5_out, bit_extender_6_out, bit_extender_7_out, comparator_1_gt, comparator_2_gt,
       multiplier_1_out, or_2_out, xor_2_out;

  Multiplexer #(.select(4), .width(16)) multiplexer_1 (
    .in1(bit_extender_1_out), .in2(bit_extender_2_out), .in3(multiplier_1_out), .in4(bit_extender_3_out),
    .in5(bit_extender_4_out), .in6(and_2_out), .in7(bit_extender_5_out), .in8(or_2_out),
    .in9(bit_extender_6_out), .in10(bit_extender_7_out), .in11(xor_2_out), .in12(comparator_1_gt),
    .in13(comparator_2_gt), .out(Y), .sel(O));  // open: in0, in14, in15
  Pull_Resistor pull_resistor_1 (.node(A));
  Pull_Resistor pull_resistor_2 (.node(B));
  Adder adder_1 (.a(A[7:0]), .b(B[7:0]), .out(adder_1_out));  // open: cin, cout
  assign bit_extender_1_out = {{8{1'b0}}, adder_1_out};  // Bit_Extender bit_extender_1
  Subtractor subtractor_1 (.a(A[7:0]), .b(B[7:0]), .out(subtractor_1_out));  // open: bin, bout
  assign bit_extender_2_out = {{8{1'b0}}, subtractor_1_out};  // Bit_Extender bit_extender_2
  Multiplier multiplier_1 (
    .a(A[7:0]), .b(B[7:0]), .out(multiplier_1_out[7:0]), .cout(multiplier_1_out[15:8]));  // open: cin
  assign bit_extender_3_out = {{8{1'b0}}, divider_1_out};  // Bit_Extender bit_extender_3
  Divider divider_1 (.a(A[7:0]), .b(B[7:0]), .out(divider_1_out));  // open: upper, rem
  assign and_1_out = A[7:0] & B[7:0];  // AND_Gate and_1, 8 bits wide
  assign and_2_out = A & B;  // AND_Gate and_2, 16 bits wide
  assign bit_extender_4_out = {{8{1'b0}}, and_1_out};  // Bit_Extender bit_extender_4
  assign or_1_out = A[7:0] | B[7:0];  // OR_Gate or_1, 8 bits wide
  assign or_2_out = A | B;  // OR_Gate or_2, 16 bits wide
  assign bit_extender_5_out = {{8{1'b0}}, or_1_out};  // Bit_Extender bit_extender_5
  assign not_1_out = ~A[7:0];  // NOT_Gate not_1, 8 bits wide
  assign xor_1_out = A[7:0] ^ B[7:0];  // XOR_Gate xor_1, 8 bits wide
  assign bit_extender_6_out = {{8{1'b0}}, not_1_out};  // Bit_Extender bit_extender_6
  assign bit_extender_7_out = {{8{1'b0}}, xor_1_out};  // Bit_Extender bit_extender_7
  assign xor_2_out = A ^ B;  // XOR_Gate xor_2, 16 bits wide
  Comparator #(.mode("unsigned")) comparator_1 (
    .a(A[7:0]), .b(B[7:0]), .gt(comparator_1_gt[0]), .eq(comparator_1_gt[1]), .lt(comparator_1_gt[2]));
  Pull_Resistor pull_resistor_3 (.node(Y));
  Comparator #(.mode("unsigned"), .width(16)) comparator_2 (
    .a(A), .b(B), .gt(comparator_2_gt[0]), .eq(comparator_2_gt[1]), .lt(comparator_2_gt[2]));

  // Notes on the sheet:
  //   my eyes hurt
endmodule

module register_file (
);

  Register x0 ();  // open: D, en, clk, Q, clr
  Register x4 ();  // open: D, en, clk, Q, clr
  Register x8 ();  // open: D, en, clk, Q, clr
  Register xc ();  // open: D, en, clk, Q, clr
  Register x1 ();  // open: D, en, clk, Q, clr
  Register x5 ();  // open: D, en, clk, Q, clr
  Register x9 ();  // open: D, en, clk, Q, clr
  Register xd ();  // open: D, en, clk, Q, clr
  Register x2 ();  // open: D, en, clk, Q, clr
  Register x6 ();  // open: D, en, clk, Q, clr
  Register xa ();  // open: D, en, clk, Q, clr
  Register xe ();  // open: D, en, clk, Q, clr
  Register x3 ();  // open: D, en, clk, Q, clr
  Register x7 ();  // open: D, en, clk, Q, clr
  Register xb ();  // open: D, en, clk, Q, clr
  Register xf ();  // open: D, en, clk, Q, clr
endmodule
